# Fritzing sketch draft (saved by Fritzing 0.9.4)

parts:
  WeMos_D1_Mini1 = WeMos D1 Mini
  M1 = BME280
  SDS1 = SDS011 - dust sensor [part_number=1]
  VCC1 = Battery
  Part1 = step-up
  C1 = Electrolytic Capacitor [capacitance=0.22mF voltage=16V package="0405 [SMD, electrolytic]"]
  C2 = Electrolytic Capacitor [capacitance=0.22mF voltage=16V package="0405 [SMD, electrolytic]"]

nets:
  3V3: WeMos_D1_Mini1.3V3, M1.VIN
  5V: WeMos_D1_Mini1.5V, SDS1.5v, Part1.VOUT, C2.+
  N1: WeMos_D1_Mini1.A0, VCC1.+, Part1.VIN, C1.+
  N2: WeMos_D1_Mini1.D1, M1.SCL
  N3: WeMos_D1_Mini1.D2, M1.SDA
  GND: WeMos_D1_Mini1.G, M1.GND, SDS1.GND, VCC1.-, Part1.GND, C1.-, C2.-
  N4: WeMos_D1_Mini1.RX, SDS1.TX

custom parts:
  BME280: Temperature Humidity Barometric presure Sensor
  SDS011 - dust sensor: The SDS 011 Sensor is a quite recent Air Quality Sensor developed by inovafit, a spin-off from the university of Jinan (in Shandong). With its size, it is probably one of the best sensor in terms of accuracy: While other sensors tend to focus on shrinking the sensor size, the SDS 011 has opted for a size tradeoff allowing it to use a larger fan. And the larger the fan, the better the quality.
  step-up: Description: The NCP1400 is a 3.3V DC-DC converter. The breakout board will accept voltage inputs between 1 and 3 Volts (such as 1 or 2 AA batteries) and output a constant, low ripple 3.3V output capable of sourcing up to 100 mA. This board is great for supplying power to 3.3V sensors or providing 3.3V from a a single AA battery. The breakout board includes the necessary peripheral components.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
